# Fritzing sketch pictorico (saved by Fritzing 0.9.3b)

parts:
  Componente1 = Dimmer + Wemos + Fuente switching
  BULB2 = LEDs [package=led10mm]  # not connected
  BULB4 = Incandescent light bulb small [package="bulb sm"]
  WeMos_D1_Mini1 = WeMos D1 Mini

nets:
  N1: Componente1.AC-IN-FASE, WeMos_D1_Mini1.Neutro
  N2: Componente1.AC-IN-NEUTRO, WeMos_D1_Mini1.Fase
  N3: Componente1.CARGA-FASE, BULB4.1
  N4: Componente1.CARGA-NEUTRO, BULB4.2

custom parts:
  Dimmer + Wemos + Fuente switching: https://github.com/lu4ult/dimmer-modulo-desarrollo
  WeMos D1 Mini: The D1 mini is a mini wifi board based on ESP-8266EX.
