# Fritzing sketch Encoder Fritzing (saved by Fritzing 0.9.3b)

parts:
  Componente1 = Dimmer + Wemos + Fuente switching
  BULB2 = LEDs [package=led10mm]  # not connected
  BULB4 = Incandescent light bulb small [package="bulb sm"]
  WeMos_D1_Mini1 = WeMos D1 Mini
  RE2 = KY-040 Rotary encoder [package=THT]

nets:
  +5V: Componente1.+5V, RE2.Vcc
  N1: Componente1.D7, RE2.SW
  N2: Componente1.SDA, RE2.DT
  N3: Componente1.AC-IN-FASE, WeMos_D1_Mini1.Neutro
  N4: Componente1.AC-IN-NEUTRO, WeMos_D1_Mini1.Fase
  N5: Componente1.CARGA-FASE, BULB4.1
  N6: Componente1.CARGA-NEUTRO, BULB4.2
  N7: Componente1.GND#19, RE2.GND
  N8: Componente1.GND#d1, RE2.CLK

custom parts:
  Dimmer + Wemos + Fuente switching: https://github.com/lu4ult/dimmer-modulo-desarrollo
  WeMos D1 Mini: The D1 mini is a mini wifi board based on ESP-8266EX.
  KY-040 Rotary encoder: KY-040 Rotary Encoder with switch on breakout borad from AZ Delivery
