# Fritzing sketch Pulsador pictorico (saved by Fritzing 0.9.3b)

parts:
  Componente1 = Dimmer + Wemos + Fuente switching
  BULB2 = LEDs [package=led10mm]  # not connected
  BULB4 = Incandescent light bulb small [package="bulb sm"]
  WeMos_D1_Mini1 = WeMos D1 Mini
  S1 = Pushbutton [package="[THT]"]
  BULB5 = Incandescent light bulb small [package="bulb sm"]
  WeMos_D1_Mini2 = WeMos D1 Mini
  BULB6 = LEDs [package=led10mm]  # not connected
  Componente2 = Dimmer + Wemos + Fuente switching
  S3 = Toggle Switch [package=THT]

nets:
  N1: Componente1.AC-IN-FASE, WeMos_D1_Mini1.Neutro
  N2: Componente1.AC-IN-NEUTRO, WeMos_D1_Mini1.Fase
  N3: Componente1.CARGA-FASE, BULB4.1
  N4: Componente1.CARGA-NEUTRO, BULB4.2
  N5: Componente1.GND, S1.Pin_1, S1.Pin_2
  N6: Componente1.D4, S1.Pin_3
  N7: BULB5.1, Componente2.CARGA-FASE
  N8: BULB5.2, Componente2.CARGA-NEUTRO
  N9: WeMos_D1_Mini2.Neutro, Componente2.AC-IN-FASE
  N10: WeMos_D1_Mini2.Fase, Componente2.AC-IN-NEUTRO
  N11: Componente2.GND, S3.COM
  N12: Componente2.D4, S3.L2

notes:
  LLAVE O TECLA
  PULSADOR O BOTÓN

custom parts:
  Dimmer + Wemos + Fuente switching: https://github.com/lu4ult/dimmer-modulo-desarrollo
  WeMos D1 Mini: The D1 mini is a mini wifi board based on ESP-8266EX.
